# Fritzing sketch arduboy_fritz (saved by Fritzing 0.9.9b)
breadboards: 2

parts:
  Part2 = SPI OLED Monochrome 128x64 0.96 inch
  J1 = Piezo Speaker
  S1 = Pushbutton [package="[THT]"]
  S2 = Pushbutton [package="[THT]"]
  S3 = Pushbutton [package="[THT]"]
  S4 = Pushbutton [package="[THT]"]
  S5 = Pushbutton [package="[THT]"]
  S6 = Pushbutton [package="[THT]"]
  S7 = Pushbutton [package="[THT]"]
  Part3 = Arduino Pro Micro (Clone)

nets:
  GND: Part2.GND, J1.pin1, S1.Pin_3, S1.Pin_4, S2.Pin_3, S2.Pin_4, S3.Pin_3, S3.Pin_4, S4.Pin_3, S4.Pin_4, S5.Pin_3, S5.Pin_4, S6.Pin_3, S6.Pin_4, S7.Pin_3, S7.Pin_4, Part3.GND
  VDD: Part2.VDD, Part3.VCC
  N1: Part2.SCK, Part3.D15
  N2: Part2.SDA, Part3.D16
  N3: Part2.RES, Part3.D6
  N4: Part2.DC, Part3.D4
  N5: S1.Pin_1, S1.Pin_2, Part3.A0
  N6: S2.Pin_1, S2.Pin_2, Part3.A2
  N7: S3.Pin_1, S3.Pin_2, Part3.D8
  N8: S4.Pin_1, S4.Pin_2, Part3.RST
  N9: S5.Pin_1, S5.Pin_2, Part3.A1
  N10: S6.Pin_1, S6.Pin_2, Part3.D7
  N11: S7.Pin_1, S7.Pin_2, Part3.A3

custom parts:
  SPI OLED Monochrome 128x64 0.96 inch: Unknown 128x64 0.96 inch 128x64 SPI Monochrome OLED display
